// Logisim project cpu.circ as structural Verilog: 2 circuits, main circuit main
module main (
  input  [31:0] INSTRUCTION,
  input  CLOCK,
  output [31:0] FETCH_ADDRESS,
  output [31:0] s0_Value,
  output [31:0] s1_Value,
  output [31:0] s2_Value,
  output [31:0] ra_Value,
  output [31:0] sp_Value
);

  wire ALUsrc, and_1_out, and_2_out, beq, bne, equal, ExtOp, jal, jump, jumpreg, lui, main_2_signed_overflow,
       MemtoReg, MemWr, or_1_out, or_3_out, RegDst, RegWr, shift, swinc, validbranch;
  wire [3:0] ALUctr;
  wire [4:0] multiplexer_5_out, multiplexer_6_out, multiplexer_7_out;
  wire [5:0] funct, opcode;
  wire [15:6] IMM16;
  wire [25:16] IMM26;
  wire [31:0] adder_1_out, adder_2_out, bit_extender_1_out, bit_extender_2_out, bit_extender_3_out,
       bit_extender_4_out, main_1_read_data_2, main_2_result, main_3_p5, multiplexer_1_out,
       multiplexer_2_out, multiplexer_3_out, multiplexer_4_out, multiplexer_8_out, multiplexer_9_out,
       multiplexer_10_out, multiplexer_11_out, multiplexer_12_out, multiplexer_13_out, RS_value,
       shifter_1_out;

  assign bit_extender_1_out = {{16{IMM16[15]}}, {IMM16, funct}};  // Bit_Extender bit_extender_1
  Shifter #(.width(32)) shifter_1 (.in(bit_extender_1_out), .\dist (5'b00010), .out(shifter_1_out));
  Multiplexer #(.width(32)) multiplexer_1 (
    .in0(INSTRUCTION), .in1({32{1'b0}}), .out(multiplexer_1_out), .sel(or_1_out));  // open: en
  or or_1 (or_1_out, validbranch, jal, jump, jumpreg);
  Adder #(.width(32)) adder_1 (.a(FETCH_ADDRESS), .b(32'h4), .out(adder_1_out));  // open: cin, cout
  Adder #(.width(32)) adder_2 (.a(adder_1_out), .b(shifter_1_out), .out(adder_2_out));  // open: cin, cout
  Multiplexer #(.width(32), .enable("false")) multiplexer_2 (
    .in0(adder_1_out), .in1(adder_2_out), .out(multiplexer_2_out), .sel(validbranch));
  and and_1 (and_1_out, beq, equal);
  Register #(.width(32)) register_1 (
    .D(multiplexer_1_out), .Q({opcode, IMM26, IMM16, funct}), .clk(CLOCK));  // open: en, clr
  or or_2 (validbranch, and_1_out, and_2_out);
  and and_2 (and_2_out, bne, ~equal);  // AND_Gate
  Multiplexer #(.width(32), .enable("false")) multiplexer_3 (
    .in0(multiplexer_2_out), .in1({FETCH_ADDRESS[31:28], IMM26, IMM16, funct, 2'b00}),
    .out(multiplexer_3_out), .sel(or_3_out));
  or or_3 (or_3_out, jump, jal);
  Multiplexer #(.width(32), .enable("false")) multiplexer_4 (
    .in0(multiplexer_3_out), .in1(RS_value), .out(multiplexer_4_out), .sel(jumpreg));
  Register #(.width(32)) PC (.D(multiplexer_4_out), .Q(FETCH_ADDRESS), .clk(CLOCK));  // open: en, clr
  Multiplexer #(.width(5)) multiplexer_5 (
    .in0(IMM26[20:16]), .in1(IMM16[15:11]), .out(multiplexer_5_out), .sel(RegDst));  // open: en
  Multiplexer #(.width(5)) multiplexer_6 (
    .in0(multiplexer_5_out), .in1(IMM26[25:21]), .out(multiplexer_6_out), .sel(swinc));  // open: en
  Adder #(.width(32)) adder_3 (.b(32'h4));  // open: a, out, cin, cout
  Multiplexer #(.width(5)) multiplexer_7 (
    .in0(multiplexer_6_out), .in1({5{1'b1}}), .out(multiplexer_7_out), .sel(jal));  // open: en
  controller_circ controller_circ_1 (
    .opcode(opcode), .funct(funct), .RegDst(RegDst), .RegWr(RegWr), .ExtOp(ExtOp), .ALUsrc(ALUsrc),
    .ALUctr(ALUctr), .MemWr(MemWr), .MemtoReg(MemtoReg), .beq(beq), .bne(bne), .jump(jump),
    .jumpreg(jumpreg), .lui(lui), .shift(shift), .swinc(swinc), .jal(jal));
  regfile_main main_1 (
    .Read_Register_1(IMM26[25:21]), .Read_Register_2(IMM26[20:16]), .Write_Register(multiplexer_7_out),
    .Write_Data(multiplexer_13_out), .Write_Enable(RegWr), .Clock(CLOCK), .Read_Data_1(RS_value),
    .Read_Data_2(main_1_read_data_2), .s0_Value(s0_Value), .s1_Value(s1_Value), .s2_Value(s2_Value),
    .ra_Value(ra_Value), .sp_Value(sp_Value));
  assign bit_extender_2_out = {{16{1'b0}}, {IMM16, funct}};  // Bit_Extender bit_extender_2
  assign bit_extender_3_out = {{16{IMM16[15]}}, {IMM16, funct}};  // Bit_Extender bit_extender_3
  Multiplexer #(.width(32), .enable("false")) multiplexer_8 (
    .in0(bit_extender_2_out), .in1(bit_extender_3_out), .out(multiplexer_8_out), .sel(ExtOp));
  Multiplexer #(.width(32)) multiplexer_9 (
    .in0(RS_value), .in1(32'h10), .out(multiplexer_9_out), .sel(lui));  // open: en
  Multiplexer #(.width(32)) multiplexer_10 (
    .in0(multiplexer_9_out), .in1(bit_extender_4_out), .out(multiplexer_10_out), .sel(shift));  // open: en
  assign bit_extender_4_out = {{27{1'b0}}, IMM16[10:6]};  // Bit_Extender bit_extender_4
  LED led_1 (.in(main_2_signed_overflow));
  alu_main main_2 (
    .Switch(ALUctr), .X(multiplexer_10_out), .Equal(equal), .Result(main_2_result),
    .Signed_Overflow(main_2_signed_overflow), .Y(multiplexer_11_out));
  Multiplexer #(.width(32), .enable("false")) multiplexer_11 (
    .in0(main_1_read_data_2), .in1(multiplexer_8_out), .out(multiplexer_11_out), .sel(ALUsrc));
  // mem_main main_3: pin names not known; wires that end beside it: main_2_result, main_1_read_data_2, MemWr, CLOCK, main_3_p5
  Multiplexer #(.width(32)) multiplexer_12 (
    .in0(main_2_result), .in1(FETCH_ADDRESS), .out(multiplexer_12_out), .sel(jal));  // open: en
  Multiplexer #(.width(32), .enable("false")) multiplexer_13 (
    .in0(multiplexer_12_out), .in1(main_3_p5), .out(multiplexer_13_out), .sel(MemtoReg));

  // Other names for the same wires on the sheet: IMM16[5:0] = funct; IMM26[15:0] = {IMM16, funct};
  //   shamt[4:0] = IMM16[10:6]; RD[4:0] = IMM16[15:11]; RT[4:0] = IMM26[20:16]; RS[4:0] = IMM26[25:21]; clk = CLOCK;
  //   fetch_addr[31:0] = FETCH_ADDRESS; oldPC[31:0] = FETCH_ADDRESS; top4[3:0] = FETCH_ADDRESS[31:28];
  //   ra[31:0] = ra_Value; s0[31:0] = s0_Value; s1[31:0] = s1_Value; s2[31:0] = s2_Value; sp[31:0] = sp_Value

  // Notes on the sheet:
  //   Output
  //   These are outputs/inputs from run.circ
  //   Inputs
  //   These are DEBUG/TEST outputs from your circuit.
endmodule

module controller_circ (
  input  [5:0] opcode,
  input  [5:0] funct,
  output RegDst,
  output RegWr,
  output ExtOp,
  output ALUsrc,
  output [3:0] ALUctr,
  output MemWr,
  output MemtoReg,
  output beq,
  output bne,
  output jump,
  output jumpreg,
  output lui,
  output shift,
  output swinc,
  output jal
);

  wire isadd, isaddi, isaddiu, isaddu, isand, isandi, isjr, isor, isori, issll, isslt, isslti, issltiu,
       issltu, issra, issrl, issub, issubu, issw, or_6_out, or_7_out, or_8_out, or_9_out, or_10_out,
       or_11_out;
  wire [3:0] multiplexer_1_out, multiplexer_2_out, multiplexer_3_out, multiplexer_4_out, multiplexer_5_out,
       multiplexer_6_out, multiplexer_7_out, multiplexer_8_out, multiplexer_9_out, multiplexer_10_out,
       multiplexer_11_out;

  Comparator #(.width(6)) comparator_1 (.a(opcode), .b({6{1'b0}}), .eq(RegDst));  // open: gt, lt
  and and_1 (isaddi, ~opcode[0], ~opcode[1], ~opcode[2], opcode[3], ~opcode[4], ~opcode[5]);  // AND_Gate
  and and_2 (isaddiu, opcode[0], ~opcode[1], ~opcode[2], opcode[3], ~opcode[4], ~opcode[5]);  // AND_Gate
  and and_3 (isandi, ~opcode[0], ~opcode[1], opcode[2], opcode[3], ~opcode[4], ~opcode[5]);  // AND_Gate
  and and_4 (beq, ~opcode[0], ~opcode[1], opcode[2], ~opcode[3], ~opcode[4], ~opcode[5]);  // AND_Gate
  and and_5 (bne, opcode[0], ~opcode[1], opcode[2], ~opcode[3], ~opcode[4], ~opcode[5]);  // AND_Gate
  and and_6 (jump, ~opcode[0], opcode[1], ~opcode[2], ~opcode[3], ~opcode[4], ~opcode[5]);  // AND_Gate
  and and_7 (jal, opcode[0], opcode[1], ~opcode[2], ~opcode[3], ~opcode[4], ~opcode[5]);  // AND_Gate
  and and_8 (lui, opcode[0], opcode[1], opcode[2], opcode[3], ~opcode[4], ~opcode[5]);  // AND_Gate
  and and_9 (MemtoReg, opcode[0], opcode[1], ~opcode[2], ~opcode[3], ~opcode[4], opcode[5]);  // AND_Gate
  and and_10 (isori, opcode[0], ~opcode[1], opcode[2], opcode[3], ~opcode[4], ~opcode[5]);  // AND_Gate
  and and_11 (isslti, ~opcode[0], opcode[1], ~opcode[2], opcode[3], ~opcode[4], ~opcode[5]);  // AND_Gate
  and and_12 (issltiu, opcode[0], opcode[1], ~opcode[2], opcode[3], ~opcode[4], ~opcode[5]);  // AND_Gate
  and and_13 (issw, opcode[0], opcode[1], ~opcode[2], opcode[3], ~opcode[4], opcode[5]);  // AND_Gate
  and and_14 (swinc, ~opcode[0], ~opcode[1], opcode[2], opcode[3], ~opcode[4], opcode[5]);  // AND_Gate
  and and_15 (isadd, RegDst, ~funct[0], ~funct[1], ~funct[2], ~funct[3], ~funct[4], funct[5]);  // AND_Gate
  and and_16 (isaddu, RegDst, funct[0], ~funct[1], ~funct[2], ~funct[3], ~funct[4], funct[5]);  // AND_Gate
  and and_17 (isand, RegDst, ~funct[0], ~funct[1], funct[2], ~funct[3], ~funct[4], funct[5]);  // AND_Gate
  and and_18 (isjr, RegDst, ~funct[0], ~funct[1], ~funct[2], funct[3], ~funct[4], ~funct[5]);  // AND_Gate
  and and_19 (isor, RegDst, funct[0], ~funct[1], funct[2], ~funct[3], ~funct[4], funct[5]);  // AND_Gate
  and and_20 (isslt, RegDst, ~funct[0], funct[1], ~funct[2], funct[3], ~funct[4], funct[5]);  // AND_Gate
  and and_21 (issltu, RegDst, funct[0], funct[1], ~funct[2], funct[3], ~funct[4], funct[5]);  // AND_Gate
  and and_22 (issll, RegDst, ~funct[0], ~funct[1], ~funct[2], ~funct[3], ~funct[4], ~funct[5]);  // AND_Gate
  and and_23 (issra, RegDst, funct[0], funct[1], ~funct[2], ~funct[3], ~funct[4], ~funct[5]);  // AND_Gate
  and and_24 (issrl, RegDst, ~funct[0], funct[1], ~funct[2], ~funct[3], ~funct[4], ~funct[5]);  // AND_Gate
  and and_25 (issub, RegDst, ~funct[0], funct[1], ~funct[2], ~funct[3], ~funct[4], funct[5]);  // AND_Gate
  and and_26 (issubu, RegDst, funct[0], funct[1], ~funct[2], ~funct[3], ~funct[4], funct[5]);  // AND_Gate
  and and_27 (jumpreg, RegDst, ~funct[0], ~funct[1], ~funct[2], funct[3], ~funct[4], ~funct[5]);  // AND_Gate
  or or_1 (RegWr, swinc, isaddiu, isori, RegDst, isaddi, isandi, MemtoReg, isslti, issltiu, jal);
  or or_2 (ExtOp, isaddiu, MemtoReg, isaddi, swinc, isslti, issltiu, issw);
  or or_3 (ALUsrc, isaddiu, issw, isori, isaddi, swinc, isandi, MemtoReg, isslti, issltiu);
  or or_4 (MemWr, issw, swinc);
  or or_5 (shift, issll, issrl, issra);
  or or_6 (or_6_out, issw, MemtoReg, swinc, isadd, isaddi);
  or or_7 (or_7_out, isslti, isslt);
  or or_8 (or_8_out, issltiu, issltu);
  or or_9 (or_9_out, isaddu, isaddiu);
  or or_10 (or_10_out, isand, isandi);
  or or_11 (or_11_out, isor, isori);
  Multiplexer #(.width(4)) multiplexer_1 (
    .in0(4'b0000), .in1(4'b0101), .out(multiplexer_1_out), .sel(or_6_out));  // open: en
  Multiplexer #(.width(4)) multiplexer_2 (
    .in0(4'b0000), .in1(4'b1011), .out(multiplexer_2_out), .sel(or_7_out));  // open: en
  Multiplexer #(.width(4)) multiplexer_3 (
    .in0(4'b0000), .in1(4'b1100), .out(multiplexer_3_out), .sel(or_8_out));  // open: en
  Multiplexer #(.width(4)) multiplexer_4 (
    .in0(4'b0000), .in1(4'b0110), .out(multiplexer_4_out), .sel(or_9_out));  // open: en
  Multiplexer #(.width(4)) multiplexer_5 (
    .in0(4'b0000), .in1(4'b1001), .out(multiplexer_5_out), .sel(or_10_out));  // open: en
  Multiplexer #(.width(4)) multiplexer_6 (
    .in0(4'b0000), .in1(4'b1010), .out(multiplexer_6_out), .sel(or_11_out));  // open: en
  Multiplexer #(.width(4)) multiplexer_7 (
    .in0(4'b0000), .in1(4'b0000), .out(multiplexer_7_out), .sel(issll));  // open: en
  Multiplexer #(.width(4)) multiplexer_8 (
    .in0(4'b0000), .in1(4'b0010), .out(multiplexer_8_out), .sel(issra));  // open: en
  Multiplexer #(.width(4)) multiplexer_9 (
    .in0(4'b0000), .in1(4'b0001), .out(multiplexer_9_out), .sel(issrl));  // open: en
  Multiplexer #(.width(4)) multiplexer_10 (
    .in0(4'b0000), .in1(4'b0111), .out(multiplexer_10_out), .sel(issub));  // open: en
  Multiplexer #(.width(4)) multiplexer_11 (
    .in0(4'b0000), .in1(4'b1000), .out(multiplexer_11_out), .sel(issubu));  // open: en
  assign ALUctr = multiplexer_1_out | multiplexer_2_out | multiplexer_3_out | multiplexer_4_out | multiplexer_5_out | multiplexer_6_out | multiplexer_7_out | multiplexer_8_out | multiplexer_9_out | multiplexer_10_out | multiplexer_11_out;  // OR_Gate or_12, 4 bits wide

  // Other names for the same wires on the sheet: isbeq = beq; isbne = bne; isjal = jal; isjump = jump;
  //   isjumpreg = jumpreg; islui = lui; islw = MemtoReg; isrtype = RegDst; isswinc = swinc

  // Notes on the sheet:
  //   Determine the type of instruction:
  //   determine which r type instruction it is:
  //   INPUTS
  //   OUTPUTS
  //   Determine the control signals
  //   determine the ALUctr signal
endmodule
